// Logisim project lock.circ as structural Verilog: 7 circuits, main circuit Lock
module Lock (
  output Message,
  output Lock_State
);

  wire A_out, B_out, Button_Controller_2_press_output, Button_Controller_press_output,
       Button_Logic_button_output, Button_Logic_enable, Clock_out;

  Clock Clock (.out(Clock_out));
  Button A (.out(A_out));
  Button B (.out(B_out));
  Button_Controller Button_Controller (
    .Button_Input(A_out), .Clock(Clock_out), .Press_Output(Button_Controller_press_output));
  Button_Controller Button_Controller_2 (
    .Button_Input(B_out), .Clock(Clock_out), .Press_Output(Button_Controller_2_press_output));
  Button_Logic Button_Logic (
    .A_Button_Input(Button_Controller_press_output), .B_Button_Input(Button_Controller_2_press_output),
    .Button_Output(Button_Logic_button_output), .Enable(Button_Logic_enable));
  Lock_Controller Lock_Controller (
    .Button_Input(Button_Logic_button_output), .Clock(Clock_out), .Enable(Button_Logic_enable),
    .Message(Message), .Lock_State(Lock_State));
endmodule

module Lock_Controller (
  input  Button_Input,
  input  Clock,
  input  Enable,
  output Message,
  output Lock_State
);

  wire lock_logic_1_n0, lock_logic_1_n1, lock_logic_1_n2, state_register_1_p0, state_register_1_p1,
       state_register_1_p2;

  Lock_Logic lock_logic_1 (
    .p2(state_register_1_p2), .p1(state_register_1_p1), .p0(state_register_1_p0), .x(Button_Input),
    .m(Message), .n(Lock_State), .n2(lock_logic_1_n2), .n1(lock_logic_1_n1), .n0(lock_logic_1_n0));
  State_Register state_register_1 (
    .Clock(Clock), .Enable(Enable), .n2(lock_logic_1_n2), .n1(lock_logic_1_n1), .n0(lock_logic_1_n0),
    .p2(state_register_1_p2), .p1(state_register_1_p1), .p0(state_register_1_p0));
endmodule

module Lock_Logic (
  input  p2,
  input  p1,
  input  p0,
  input  x,
  output m,
  output n,
  output n2,
  output n1,
  output n0
);

  wire and_1_out, and_2_out, and_3_out, and_4_out, and_5_out, and_7_out, and_8_out, and_9_out, and_10_out,
       and_11_out, and_12_out, and_13_out, and_14_out, and_15_out, and_16_out, and_17_out, and_18_out,
       and_19_out, and_20_out, not_1_out, not_2_out, not_3_out, not_4_out;

  not not_1 (not_1_out, p1);
  not not_2 (not_2_out, p2);
  not not_3 (not_3_out, p0);
  not not_4 (not_4_out, x);
  and and_1 (and_1_out, not_1_out, not_3_out, not_4_out);
  and and_2 (and_2_out, not_1_out, p0, x);
  and and_3 (and_3_out, not_1_out, not_3_out, x);
  and and_4 (and_4_out, p2, not_3_out, not_4_out);
  and and_5 (and_5_out, not_2_out, p1, p0, not_4_out);
  and and_6 (n, p2, not_1_out, p0, not_4_out);
  and and_7 (and_7_out, p2, not_1_out);
  and and_8 (and_8_out, not_1_out, not_3_out, not_4_out);
  and and_9 (and_9_out, not_2_out, p0, x);
  and and_10 (and_10_out, not_2_out, p1, x);
  and and_11 (and_11_out, not_2_out, p1, p0);
  and and_12 (and_12_out, p2, not_3_out, not_4_out);
  and and_13 (and_13_out, not_2_out, not_4_out);
  and and_14 (and_14_out, not_3_out, not_4_out);
  and and_15 (and_15_out, not_1_out, p0);
  and and_16 (and_16_out, not_2_out, p1, not_3_out);
  and and_17 (and_17_out, not_1_out, not_3_out, x);
  and and_18 (and_18_out, p2, not_3_out, x);
  and and_19 (and_19_out, not_2_out, p1, not_3_out, not_4_out);
  and and_20 (and_20_out, p2, not_1_out, p0, not_4_out);
  or or_1 (m, and_1_out, and_2_out, and_3_out, and_4_out, and_5_out);
  or or_2 (n2, and_7_out, and_8_out, and_9_out, and_10_out, and_11_out, and_12_out);
  or or_3 (n1, and_13_out, and_14_out, and_15_out, and_16_out);
  or or_4 (n0, and_17_out, and_18_out, and_19_out, and_20_out);
endmodule

module State_Register (
  input  Clock,
  input  Enable,
  input  n2,
  input  n1,
  input  n0,
  output p2,
  output p1,
  output p0
);

  D_Flip_Flop d_ff_1 (.clk(Clock), .D(n2), .Q(p2), .en(Enable));  // open: Qn, preset, reset
  D_Flip_Flop d_ff_2 (.clk(Clock), .D(n1), .Q(p1), .en(Enable));  // open: Qn, preset, reset
  D_Flip_Flop d_ff_3 (.clk(Clock), .D(n0), .Q(p0), .en(Enable));  // open: Qn, preset, reset
endmodule

module Button_Controller (
  input  Button_Input,
  input  Clock,
  output Press_Output
);

  wire Button_Controller_Logic_next_state, d_ff_1_q;

  Button_Controller_Logic Button_Controller_Logic (
    .Activation_Input(Button_Input), .Current_State(d_ff_1_q), .Button_Press_Output(Press_Output),
    .Next_State(Button_Controller_Logic_next_state));
  D_Flip_Flop d_ff_1 (
    .clk(Clock), .D(Button_Controller_Logic_next_state), .Q(d_ff_1_q));  // open: Qn, preset, en, reset
endmodule

module Button_Logic (
  input  A_Button_Input,
  input  B_Button_Input,
  output Button_Output,
  output Enable
);

  wire not_1_out;

  not not_1 (not_1_out, A_Button_Input);
  and and_1 (Button_Output, not_1_out, B_Button_Input);
  xor xor_1 (Enable, B_Button_Input, A_Button_Input);
endmodule

module Button_Controller_Logic (
  input  Activation_Input,
  input  Current_State,
  output Button_Press_Output,
  output Next_State
);

  wire not_1_out;

  not not_1 (not_1_out, Activation_Input);
  and and_1 (Button_Press_Output, not_1_out, Current_State);

  assign Next_State = Activation_Input;
endmodule
